# Fritzing sketch dist_compare_demo (saved by Fritzing 0.8.3b)
breadboards: 1

parts:
  LED1 = LED - 5mm [color="Red (633nm)" package="5 mm [THT]"]
  part = Resistor [tolerance=±5% resistance=1k package=THT]
  part_2 = Resistor [tolerance=±5% resistance=1k package=THT]
  part_3 = Resistor [tolerance=±5% resistance=1k package=THT]
  part_4 = Resistor [tolerance=±5% resistance=1k package=THT]
  part_5 = Resistor [tolerance=±5% resistance=1k package=THT]
  part_6 = Resistor [tolerance=±5% resistance=1k package=THT]
  part_7 = Resistor [tolerance=±5% resistance=1k package=THT]
  part_8 = Resistor [tolerance=±5% resistance=1k package=THT]
  LED2 = LED - 5mm [color="Red (633nm)" package="5 mm [THT]"]
  LED3 = LED - 5mm [color="Red (633nm)" package="5 mm [THT]"]
  LED4 = LED - 5mm [color="Red (633nm)" package="5 mm [THT]"]
  LED5 = LED - 5mm [color="Red (633nm)" package="5 mm [THT]"]
  LED6 = LED - 5mm [color="Red (633nm)" package="5 mm [THT]"]
  LED7 = LED - 5mm [color="Red (633nm)" package="5 mm [THT]"]
  LED8 = LED - 5mm [color="Red (633nm)" package="5 mm [THT]"]
  part_9 = Arduino Uno (Rev3)
  Part1 = SRF05 Ultrasonic Rangefinder
  J1 = Infrared Proximity Sensor

nets:
  N1: LED1.cathode, part_9.D2
  N2: LED1.anode, part.Pin_1
  GND: part.Pin_0, part_2.Pin_0, part_3.Pin_0, part_4.Pin_0, part_5.Pin_0, part_6.Pin_0, part_7.Pin_0, part_8.Pin_0, part_9.GND, Part1.GND, J1.GND
  N3: part_2.Pin_1, LED2.anode
  N4: part_3.Pin_1, LED3.anode
  N5: part_4.Pin_1, LED4.anode
  N6: part_5.Pin_1, LED5.anode
  N7: part_6.Pin_1, LED6.anode
  N8: part_7.Pin_1, LED7.anode
  N9: part_8.Pin_1, LED8.anode
  N10: LED2.cathode, part_9.D3_PWM
  N11: LED3.cathode, part_9.D4
  N12: LED4.cathode, part_9.D5_PWM
  N13: LED5.cathode, part_9.D6_PWM
  N14: LED6.cathode, part_9.D7
  N15: LED7.cathode, part_9.D8
  N16: LED8.cathode, part_9.D9_PWM
  N17: part_9.A1, J1.Vout
  N18: part_9.ICSP_MISO, part_9.D12/MISO, Part1.Echo
  VCC: part_9.5V, Part1.VCC, J1.Vcc
  N19: part_9.ICSP_SCK, Part1.Trig
