# Fritzing sketch lightdetection_fancontrol_mosfet_demo (saved by Fritzing 0.8.3b)
breadboards: 1

parts:
  Part1 = Arduino Uno (Rev3)
  Q1 = Basic FET N-Channel [package="TO220 [THT]"]
  R1 = Resistor [tolerance=±5% resistance=1k package=THT]
  M1 = DC Motor
  R3 = Resistor [tolerance=±5% resistance=10k package=THT]
  R4 = PHOTOCELL [package=photocell]
  VCC1 = Battery block 9V
  D2 = Rectifier Diode [part_number=1N4001 package="300 mil [THT]"]

nets:
  N1: Part1.A0, R3.Pin_1, R4.P$1
  N2: Part1.GND, R3.Pin_0
  N3: Part1.D9_PWM, R1.Pin_1
  N4: Part1.5V, R4.P$2
  N5: Q1.gate, R1.Pin_0
  N6: Q1.drain, M1.pin_2, D2.anode
  N7: Q1.source, VCC1.-
  N8: M1.pin_1, VCC1.+, D2.cathode
