# Fritzing sketch fan_schematic (saved by Fritzing 0.8.3b)
breadboards: 1

parts:
  Part1 = Arduino Uno (Rev3)
  J1 = Infrared Proximity Sensor
  M1 = DC Motor
  Q1 = Basic FET N-Channel [package="TO220 [THT]"]
  R1 = Resistor [tolerance=±5% resistance=220 package=THT]

nets:
  N1: Part1.A1, J1.Vout
  N2: Part1.D3_PWM, Q1.gate, R1.Pin_1
  N3: J1.GND, Q1.source, R1.Pin_0
  N4: J1.Vcc, M1.pin_1
  N5: M1.pin_2, Q1.drain
