# Fritzing sketch photoresistor_array_demo (saved by Fritzing 0.8.3b)
breadboards: 1

parts:
  LED9 = LED - 5mm [color="Red (633nm)" package="5 mm [THT]"]
  LED10 = LED - 5mm [color="Red (633nm)" package="5 mm [THT]"]
  R9 = Resistor [tolerance=±5% resistance=330 package=THT]
  LED11 = LED - 5mm [color="Red (633nm)" package="5 mm [THT]"]
  R11 = Resistor [tolerance=±5% resistance=330 package=THT]
  LED12 = LED - 5mm [color="Red (633nm)" package="5 mm [THT]"]
  R12 = Resistor [tolerance=±5% resistance=330 package=THT]
  R13 = Resistor [tolerance=±5% resistance=330 package=THT]
  LED14 = LED - 5mm [color="Red (633nm)" package="5 mm [THT]"]
  R14 = Resistor [tolerance=±5% resistance=330 package=THT]
  LED16 = LED - 5mm [color="Red (633nm)" package="5 mm [THT]"]
  R16 = Resistor [tolerance=±5% resistance=330 package=THT]
  Part3 = Arduino Uno (Rev3)
  R18 = Photocell (LDR) [package=THT]
  R22 = Resistor [tolerance=±5% resistance=2k package=THT]
  R23 = Photocell (LDR) [package=THT]
  R24 = Resistor [tolerance=±5% resistance=2k package=THT]
  R25 = Photocell (LDR) [package=THT]
  R26 = Resistor [tolerance=±5% resistance=2k package=THT]
  R27 = Photocell (LDR) [package=THT]
  R28 = Resistor [tolerance=±5% resistance=2k package=THT]
  R29 = Photocell (LDR) [package=THT]
  R30 = Resistor [tolerance=±5% resistance=2k package=THT]
  R31 = Photocell (LDR) [package=THT]
  R32 = Resistor [tolerance=±5% resistance=2k package=THT]
  LED17 = LED - 5mm [color="Red (633nm)" package="5 mm [THT]"]
  R33 = Resistor [tolerance=±5% resistance=2k package=THT]
  LED18 = LED - 5mm [color="Red (633nm)" package="5 mm [THT]"]
  R34 = Resistor [tolerance=±5% resistance=2k package=THT]
  LED19 = LED - 5mm [color="Red (633nm)" package="5 mm [THT]"]
  R35 = Resistor [tolerance=±5% resistance=2k package=THT]

nets:
  N1: LED9.cathode, Part3.D6_PWM
  N2: LED9.anode, R13.Pin_1
  N3: LED10.cathode, Part3.D7
  N4: LED10.anode, R9.Pin_1
  N5: R9.Pin_0, R11.Pin_0, R12.Pin_0, R13.Pin_0, R14.Pin_0, R16.Pin_0, Part3.GND, R22.Pin_1, R24.Pin_1, R26.Pin_1, R28.Pin_1, R30.Pin_1, R32.Pin_1, R33.Pin_1, R34.Pin_1, R35.Pin_1
  N6: LED11.cathode, Part3.D2
  N7: LED11.anode, R12.Pin_1
  N8: R11.Pin_1, LED12.anode
  N9: LED12.cathode, Part3.D3_PWM
  N10: LED14.cathode, Part3.D5_PWM
  N11: LED14.anode, R14.Pin_1
  N12: LED16.cathode, Part3.D4
  N13: LED16.anode, R16.Pin_1
  N14: Part3.A0, R31.pin_1, R32.Pin_0
  N15: Part3.A1, R29.pin_1, R30.Pin_0
  N16: Part3.A2, R18.pin_1, R22.Pin_0
  N17: Part3.A3, R27.pin_1, R28.Pin_0
  N18: Part3.A4/SDA, R25.pin_1, R26.Pin_0
  N19: Part3.A5/SCL, R23.pin_1, R24.Pin_0
  N20: Part3.5V, R18.pin_0, R23.pin_0, R25.pin_0, R27.pin_0, R29.pin_0, R31.pin_0, LED17.anode, LED18.anode, LED19.anode
  N21: LED17.cathode, R33.Pin_0
  N22: LED18.cathode, R34.Pin_0
  N23: LED19.cathode, R35.Pin_0
