# Fritzing sketch servo_schematic (saved by Fritzing 0.8.3b)
breadboards: 1

parts:
  Part1 = Arduino Uno (Rev3)
  J1 = Basic Servo
  LED1 = LED - 5mm [color="Red (633nm)" package="5 mm [THT]"]
  S1 = Pushbutton [package="[THT]"]
  S2 = Pushbutton [package="[THT]"]
  R1 = Resistor [tolerance=±5% resistance=220 package=THT]
  R2 = Resistor [package="2512 [SMD]"]
  R3 = Resistor [package="2512 [SMD]"]

nets:
  N1: Part1.D11_PWM/MOSI, J1.pulse
  N2: Part1.D3_PWM, LED1.cathode
  N3: Part1.D4, S2.Pin_1, S2.Pin_2, R3.Pin_0
  N4: J1.gnd, R1.Pin_1, R2.Pin_1, R3.Pin_1
  N5: J1.vcc, S1.Pin_3, S1.Pin_4, S2.Pin_3, S2.Pin_4
  N6: LED1.anode, R1.Pin_0
  N7: S1.Pin_1, S1.Pin_2, R2.Pin_0
