# Fritzing sketch schematic (saved by Fritzing 0.8.3b)
breadboards: 1

parts:
  Part1 = Arduino Uno (Rev3)
  R1 = Resistor [tolerance=±5% resistance=1k package=THT]
  J1 = Infrared Proximity Sensor
  J3 = Basic Servo
  LED1 = LED - 5mm [color="Red (633nm)" package="5 mm [THT]"]
  J4 = Basic Servo

nets:
  N1: Part1.A1, J1.GND
  VCC: Part1.5V, J1.Vcc, J3.vcc, J4.vcc
  GND: Part1.GND, R1.Pin_1, J1.Vout, J3.gnd, J4.gnd
  N2: Part1.D9_PWM, R1.Pin_0, LED1.anode
  N3: Part1.D5_PWM, J4.pulse
  N4: Part1.D6_PWM, J3.pulse
