# Fritzing sketch mosfet_led (saved by Fritzing 0.6.3b)
breadboards: 1

parts:
  N-channel_MOSFET = Basic FET N-Channel [package="TO220 [THT]"]
  LED = LED - 5mm [color="Red (633nm)" package="5 mm [THT]"]
  Resistor = Resistor [tolerance=±5% resistance=1k package=THT]
  Battery = Battery_block_9V

nets:
  N1: N-channel_MOSFET.gate, N-channel_MOSFET.source, Battery.connector0
  N2: N-channel_MOSFET.drain, Resistor.Pin_1
  N3: LED.cathode, Resistor.Pin_0
  N4: LED.anode, Battery.connector1
