# Fritzing sketch pot_voltage_divider (saved by Fritzing 0.6.3b)
breadboards: 1

parts:
  Potentiometer = Rotary Potentiometer (Small) [maximum_resistance=10kΩ]
  Resistor = Resistor [tolerance=±5% resistance=10k package=THT]
  Battery = Battery block 9V

nets:
  N1: Potentiometer.wiper, Resistor.Pin_1
  N2: Potentiometer.leg2, Battery.-
  N3: Resistor.Pin_0, Battery.+
