# Fritzing sketch pot_voltage_divider_mosfet_led_combined (saved by Fritzing 0.6.3b)
breadboards: 1

parts:
  N-channel_MOSFET = Basic FET N-Channel [package="TO220 [THT]"]
  LED = LED - 5mm [color="Red (633nm)" package="5 mm [THT]"]
  R2 = Resistor [tolerance=±5% resistance=1k package=THT]
  Battery = Battery_block_9V
  Pot = Rotary Potentiometer (Small) [maximum_resistance=10kΩ]
  R1 = Resistor [tolerance=±5% resistance=10k package=THT]

nets:
  N1: N-channel_MOSFET.gate, Pot.wiper, R1.Pin_1
  N2: N-channel_MOSFET.drain, R2.Pin_1
  N3: N-channel_MOSFET.source, Battery.connector0, Pot.leg2
  N4: LED.cathode, R2.Pin_0
  N5: LED.anode, Battery.connector1, R1.Pin_0
